# Fritzing sketch UDOOMediaServer-v2 (saved by Fritzing 0.8.3b)
breadboards: 4

parts:
  Part2 = Arduino Due (Rev2b)
  LCD2 = LCD screen
  R14 = Resistor [tolerance=±5% resistance=4.7k package=THT]
  R15 = Resistor [tolerance=±5% resistance=56 package=THT]
  R16 = Temperature Sensor (Thermistor) [thermistor_type=NTC package=THT]
  R17 = Resistor [tolerance=±5% resistance=10k package=THT]
  S1 = Pushbutton [package="[THT]"]
  R18 = Resistor [tolerance=±5% resistance=1 package=THT]
  Q2 = NPN-Transistor [part_number=2N2222 package="TO92 [THT]"]
  U2 = RELAY [package=relay-jzc]
  D2 = Rectifier Diode [part_number=1N4001 package="300 mil [THT]"]
  M2 = DC Motor

nets:
  N1: Part2.A0, R16.pin_1, R17.Pin_0
  N2: Part2.IOREF, R16.pin_0
  5V: Part2.5V, LCD2.VDD, U2.COIL1, D2.cathode
  GND: Part2.GND, Part2.D11_PWM, LCD2.VSS, LCD2.LED-, R14.Pin_0, R17.Pin_1, S1.Pin_1, S1.Pin_2, S1.Pin_3, S1.Pin_4, Q2.C, M2.pin_2
  N3: Part2.VIN, U2.MAIN
  N4: Part2.D8_PWM, LCD2.R/W
  N5: Part2.D9_PWM, LCD2.RS
  N6: Part2.D12_PWM, R18.Pin_1
  N7: Part2.D2_PWM, R15.Pin_1
  N8: Part2.D3_PWM, LCD2.DB7
  N9: Part2.D4_PWM/SS1, LCD2.DB6
  N10: Part2.D5_PWM, LCD2.DB5
  N11: Part2.D6_PWM, LCD2.DB4
  N12: Part2.D7_PWM, LCD2.E
  N13: LCD2.V0, R14.Pin_1
  N14: LCD2.LED+, R15.Pin_0
  N15: R18.Pin_0, Q2.B
  N16: Q2.E, U2.COIL2, D2.anode
  N17: U2.NO, M2.pin_1

notes:
  Fan
  Notes:
  - All ground is common
  - 3.3V is ref. voltage for thermistor
  - 5V is used for LCD and relay trigger
  - 12V is used for fan
  Wire:
  Yellow - 12V
  Red - 5V
  White - 3.3V
  Black - Ground
  Blue - Other/data
